# Fritzing sketch blink (saved by Fritzing 0.9.4)
breadboards: 1

parts:
  Part1 = Arduino Uno (Rev3)
  LED1 = LED - 5mm [color="Red (633nm)" package="5 mm [THT]"]
  S1 = Pushbutton [package="[THT]"]

nets:
  N1: Part1.D13/SCK, LED1.anode
  N2: Part1.GND, Part1.D2, LED1.cathode, S1.Pin_3, S1.Pin_4

notes:
  standard LED hook up with ground to the - pin
  the "switch"which is backward so we could learn about INPUT_PULLUP pinMode, high when the jumper/switch is disconnected, and low when connected
  the pressed/not-pressed state swap is explained in the code
  pin 13 goes to LED L or an external LED
